# Fritzing sketch electronic_design (saved by Fritzing 0.9.2b)
breadboards: 1

parts:
  RF1 = nRF8001 Bluetooth LE Breakout
  ARDUINO1 = Arduino Micro

nets:
  N1: RF1.SCK, ARDUINO1.SCK
  N2: RF1.MISO, ARDUINO1.MOSI
  N3: RF1.MOSI, ARDUINO1.MISO
  N4: RF1.REQ, ARDUINO1.D10
  N5: RF1.RDY, ARDUINO1.D2
  N6: RF1.RST, ARDUINO1.D9
  N7: RF1.GND, ARDUINO1.GND#31
  VIN: RF1.VIN, ARDUINO1.5V

custom parts:
  nRF8001 Bluetooth LE Breakout: nRF8001 Breakout Board
  Arduino Micro: Arduino Micro Microcontroller
